# Fritzing sketch MMA8451 (saved by Fritzing 0.9.3b)
circuit board: 5.3246cm x 2.27659cm
breadboards: 1

parts:
  Raspberry_Pi_1 = Raspberry Pi 3 [part_number=RPI-3-V1.2]
  JP1 = Header 12 [package=1x12_machine-pin-header_lock.004]

nets:
  N1: Raspberry_Pi_1.3v3, JP1.1
  N2: Raspberry_Pi_1.GPIO2, JP1.7
  N3: Raspberry_Pi_1.GPIO3, JP1.6
  N4: Raspberry_Pi_1.GND, JP1.2, JP1.8
